// Logisim project 4Bit-Serial-Adder.circ as structural Verilog: 4 circuits, main circuit 4BIT ADDER
module main (
  input  K,
  input  Clock,
  input  J,
  output Q,
  output Q_prime
);

  wire and_1_out, and_2_out;

  and and_1 (and_1_out, Q, K, Clock);
  and and_2 (and_2_out, Clock, J, Q_prime);
  nor nor_1 (Q, and_1_out, Q_prime);
  nor nor_2 (Q_prime, Q, and_2_out);
endmodule

module _4BIT_ADDER (
  input  A,
  input  B,
  output out_3,
  output out_4,
  output out_5,
  output out_6
);

  wire clock_1_out, full_adder_1_cout, full_adder_1_s, main_1_q, not_1_out, shift_register_1_q,
       shift_register_2_q;

  Clock clock_1 (.out(clock_1_out));
  shift_register shift_register_1 (.J(A), .Q(shift_register_1_q), .Clock(clock_1_out));  // open: Q1, Q2, Q3, Q4
  shift_register shift_register_2 (.J(B), .Q(shift_register_2_q), .Clock(clock_1_out));  // open: Q1, Q2, Q3, Q4
  not not_1 (not_1_out, full_adder_1_cout);
  main main_1 (.K(not_1_out), .Clock(clock_1_out), .J(full_adder_1_cout), .Q(main_1_q));  // open: Q_prime
  FULL_ADDER full_adder_1 (
    .A(shift_register_1_q), .B(shift_register_2_q), .Cin(main_1_q), .S(full_adder_1_s),
    .Cout(full_adder_1_cout));
  shift_register shift_register_3 (
    .J(full_adder_1_s), .Clock(clock_1_out), .Q1(out_3), .Q2(out_4), .Q3(out_5), .Q4(out_6));  // open: Q
endmodule

module shift_register (
  input  J,
  input  Clock,
  output Q1,
  output Q2,
  output Q3,
  output Q4,
  output Q
);

  wire main_1_q_prime, main_2_q_prime, main_3_q_prime, not_1_out;

  not not_1 (not_1_out, J);
  main main_1 (.K(not_1_out), .Clock(Clock), .J(J), .Q(Q1), .Q_prime(main_1_q_prime));
  main main_2 (.K(main_1_q_prime), .Clock(Clock), .J(Q1), .Q(Q2), .Q_prime(main_2_q_prime));
  main main_3 (.K(main_2_q_prime), .Clock(Clock), .J(Q2), .Q(Q3), .Q_prime(main_3_q_prime));
  main main_4 (.K(main_3_q_prime), .Clock(Clock), .J(Q3), .Q(Q));  // open: Q_prime

  assign Q4 = Q;
endmodule

module FULL_ADDER (
  input  A,
  input  B,
  input  Cin,
  output S,
  output Cout
);

  wire and_1_out, and_2_out, xor_1_out;

  xor xor_1 (xor_1_out, A, B);
  and and_1 (and_1_out, A, B);
  xor xor_2 (S, xor_1_out, Cin);
  and and_2 (and_2_out, xor_1_out, Cin);
  or or_1 (Cout, and_2_out, and_1_out);
endmodule
